// Digital circuit 28c16_DisplayOut.dig as structural Verilog
// 16K (2K x 8) Parallel EEPROM;
// DATA Polling for End of Write Detection not implemented!
module _28c16_DisplayOut (
  input  A0,
  input  A1,
  input  A2,
  input  A3,
  input  A4,
  input  A5,
  input  A6,
  input  A7,
  input  A8,
  input  A9,
  input  A10,
  input  nCE,
  input  nOE,
  input  nWE,
  input  VCC,
  input  GND,
  input  I_O0,
  input  I_O1,
  input  I_O2,
  input  I_O3,
  input  I_O4,
  input  I_O5,
  input  I_O6,
  input  I_O7
);

  wire nor_1_out;
  wire [7:0] _28C16_DISPLAY_d;

  EEPROM #(.AddrBits(11), .Bits(8)) _28C16_DISPLAY (
    .A({A10, A9, A8, A7, A6, A5, A4, A3, A2, A1, A0}), .CS(~nCE), .WE(~nWE), .OE(~nOE), .D(_28C16_DISPLAY_d));
  nor nor_1 (nor_1_out, nCE, ~nWE, nOE);  // NOr
  BusSplitter #(.Bits(8)) bussplitter_1 (
    .D(_28C16_DISPLAY_d), .OE(nor_1_out), .D0(I_O0), .D1(I_O1), .D2(I_O2), .D3(I_O3), .D4(I_O4), .D5(I_O5),
    .D6(I_O6), .D7(I_O7));
  PowerSupply powersupply_1 (.VDD(VCC), .GND(GND));

  // Notes on the sheet:
  //   A0: pin 8
  //   A1: pin 7
  //   A2: pin 6
  //   A3: pin 5
  //   A4: pin 4
  //   A5: pin 3
  //   A6: pin 2
  //   A7: pin 1
  //   A8: pin 23
  //   A9: pin 22
  //   A10: pin 19
  //   nCE: pin 18, default 1
  //   nOE: pin 20, default 1
  //   nWE: pin 21, default 1
  //   VCC: pin 24, default 1
  //   GND: pin 12
  //   I_O0: pin 9
  //   I_O1: pin 10
  //   I_O2: pin 11
  //   I_O3: pin 13
  //   I_O4: pin 14
  //   I_O5: pin 15
  //   I_O6: pin 16
  //   I_O7: pin 17
  //   contents of _28C16_DISPLAY (hex, n*v repeats v):
  //   7e,30,6d,79,33,5b,5f,70,7f,7b,7e,30,6d,79,33,5b,5f,70,7f,7b,7e,30,6d,79,33,5b,5f,
  //   70,7f,7b,7e,30,6d,79,33,5b,5f,70,7f,7b,7e,30,6d,79,33,5b,5f,70,7f,7b,7e,30,6d,79,
  //   33,5b,5f,70,7f,7b,7e,30,6d,79,33,5b,5f,70,7f,7b,7e,30,6d,79,33,5b,5f,70,7f,7b,7e,
  //   30,6d,79,33,5b,5f,70,7f,7b,7e,30,6d,79,33,5b,5f,70,7f,7b,7e,30,6d,79,33,5b,5f,70,
  //   7f,7b,7e,30,6d,79,33,5b,5f,70,7f,7b,7e,30,6d,79,33,5b,5f,70,7f,7b,7e,30,6d,79,33,
  //   5b,5f,70,7f,7b,7e,30,6d,79,33,5b,5f,70,7f,7b,7e,30,6d,79,33,5b,5f,70,7f,7b,7e,30,
  //   6d,79,33,5b,5f,70,7f,7b,7e,30,6d,79,33,5b,5f,70,7f,7b,7e,30,6d,79,33,5b,5f,70,7f,
  //   7b,7e,30,6d,79,33,5b,5f,70,7f,7b,7e,30,6d,79,33,5b,5f,70,7f,7b,7e,30,6d,79,33,5b,
  //   5f,70,7f,7b,7e,30,6d,79,33,5b,5f,70,7f,7b,7e,30,6d,79,33,5b,5f,70,7f,7b,7e,30,6d,
  //   79,33,5b,5f,70,7f,7b,7e,30,6d,79,33,5b,7e,7e,7e,7e,7e,7e,7e,7e,7e,7e,30,30,30,30,
  //   30,30,30,30,30,30,6d,6d,6d,6d,6d,6d,6d,6d,6d,6d,79,79,79,79,79,79,79,79,79,79,33,
  //   33,33,33,33,33,33,33,33,33,5b,5b,5b,5b,5b,5b,5b,5b,5b,5b,5f,5f,5f,5f,5f,5f,5f,5f,
  //   5f,5f,70,70,70,70,70,70,70,70,70,70,7f,7f,7f,7f,7f,7f,7f,7f,7f,7f,7b,7b,7b,7b,7b,
  //   7b,7b,7b,7b,7b,7e,7e,7e,7e,7e,7e,7e,7e,7e,7e,30,30,30,30,30,30,30,30,30,30,6d,6d,
  //   6d,6d,6d,6d,6d,6d,6d,6d,79,79,79,79,79,79,79,79,79,79,33,33,33,33,33,33,33,33,33,
  //   33,5b,5b,5b,5b,5b,5b,5b,5b,5b,5b,5f,5f,5f,5f,5f,5f,5f,5f,5f,5f,70,70,70,70,70,70,
  //   70,70,70,70,7f,7f,7f,7f,7f,7f,7f,7f,7f,7f,7b,7b,7b,7b,7b,7b,7b,7b,7b,7b,7e,7e,7e,
  //   7e,7e,7e,7e,7e,7e,7e,30,30,30,30,30,30,30,30,30,30,6d,6d,6d,6d,6d,6d,6d,6d,6d,6d,
  //   79,79,79,79,79,79,79,79,79,79,33,33,33,33,33,33,33,33,33,33,5b,5b,5b,5b,5b,5b,7e,
  //   7e,7e,7e,7e,7e,7e,7e,7e,7e,7e,7e,7e,7e,7e,7e,7e,7e,7e,7e,7e,7e,7e,7e,7e,7e,7e,7e,
  //   7e,7e,7e,7e,7e,7e,7e,7e,7e,7e,7e,7e,7e,7e,7e,7e,7e,7e,7e,7e,7e,7e,7e,7e,7e,7e,7e,
  //   7e,7e,7e,7e,7e,7e,7e,7e,7e,7e,7e,7e,7e,7e,7e,7e,7e,7e,7e,7e,7e,7e,7e,7e,7e,7e,7e,
  //   7e,7e,7e,7e,7e,7e,7e,7e,7e,7e,7e,7e,7e,7e,7e,7e,7e,7e,30,30,30,30,30,30,30,30,30,
  //   30,30,30,30,30,30,30,30,30,30,30,30,30,30,30,30,30,30,30,30,30,30,30,30,30,30,30,
  //   30,30,30,30,30,30,30,30,30,30,30,30,30,30,30,30,30,30,30,30,30,30,30,30,30,30,30,
  //   30,30,30,30,30,30,30,30,30,30,30,30,30,30,30,30,30,30,30,30,30,30,30,30,30,30,30,
  //   30,30,30,30,30,30,30,30,30,30,6d,6d,6d,6d,6d,6d,6d,6d,6d,6d,6d,6d,6d,6d,6d,6d,6d,
  //   6d,6d,6d,6d,6d,6d,6d,6d,6d,6d,6d,6d,6d,6d,6d,6d,6d,6d,6d,6d,6d,6d,6d,6d,6d,6d,6d,
  //   6d,6d,6d,6d,6d,6d,6d,6d,6d,6d,6d,6d,0,0,0,0,0,0,0,0,0,0,0,0,0,0,0,0,0,0,0,0,0,0,0,
  //   0,0,0,0,0,0,0,0,0,0,0,0,0,0,0,0,0,0,0,0,0,0,0,0,0,0,0,0,0,0,0,0,0,0,0,0,0,0,0,0,0,
  //   0,0,0,0,0,0,0,0,0,0,0,0,0,0,0,0,0,0,0,0,0,0,0,0,0,0,0,0,0,0,0,0,0,0,0,0,0,0,0,0,0,
  //   0,0,0,0,0,0,0,0,0,0,0,0,0,0,0,0,0,0,0,0,0,0,0,0,0,0,0,0,0,0,0,0,0,0,0,0,0,0,0,0,0,
  //   0,0,0,0,0,0,0,0,0,0,0,0,0,0,0,0,0,0,0,0,0,0,0,0,0,0,0,0,0,0,0,0,0,0,0,0,0,0,0,0,0,
  //   0,0,0,0,0,0,0,0,0,0,0,0,0,0,0,0,0,0,0,0,0,0,0,0,0,0,0,0,0,0,0,0,0,0,0,0,0,0,0,0,0,
  //   0,0,0,0,0,0,0,0,0,0,0,0,0,0,0,0,0,0,0,0,0,0,0,0,0,0,0,0,7f,70,5f,5b,33,79,6d,30,7e,
  //   7b,7f,70,5f,5b,33,79,6d,30,7e,7b,7f,70,5f,5b,33,79,6d,30,7e,7b,7f,70,5f,5b,33,79,
  //   6d,30,7e,7b,7f,70,5f,5b,33,79,6d,30,7e,7b,7f,70,5f,5b,33,79,6d,30,7e,7b,7f,70,5f,
  //   5b,33,79,6d,30,7e,7b,7f,70,5f,5b,33,79,6d,30,7e,7b,7f,70,5f,5b,33,79,6d,30,7e,7b,
  //   7f,70,5f,5b,33,79,6d,30,7e,7b,7f,70,5f,5b,33,79,6d,30,7e,7b,7f,70,5f,5b,33,79,6d,
  //   30,7e,7b,7f,70,5f,5b,33,79,6d,30,7e,30,6d,79,33,5b,5f,70,7f,7b,7e,30,6d,79,33,5b,
  //   5f,70,7f,7b,7e,30,6d,79,33,5b,5f,70,7f,7b,7e,30,6d,79,33,5b,5f,70,7f,7b,7e,30,6d,
  //   79,33,5b,5f,70,7f,7b,7e,30,6d,79,33,5b,5f,70,7f,7b,7e,30,6d,79,33,5b,5f,70,7f,7b,
  //   7e,30,6d,79,33,5b,5f,70,7f,7b,7e,30,6d,79,33,5b,5f,70,7f,7b,7e,30,6d,79,33,5b,5f,
  //   70,7f,7b,7e,30,6d,79,33,5b,5f,70,7f,7b,7e,30,6d,79,33,5b,5f,70,7f,7b,7e,30,6d,79,
  //   33,5b,5f,70,6d,6d,6d,6d,6d,6d,6d,6d,6d,30,30,30,30,30,30,30,30,30,30,7e,7e,7e,7e,
  //   7e,7e,7e,7e,7e,7e,7b,7b,7b,7b,7b,7b,7b,7b,7b,7b,7f,7f,7f,7f,7f,7f,7f,7f,7f,7f,70,
  //   70,70,70,70,70,70,70,70,70,5f,5f,5f,5f,5f,5f,5f,5f,5f,5f,5b,5b,5b,5b,5b,5b,5b,5b,
  //   5b,5b,33,33,33,33,33,33,33,33,33,33,79,79,79,79,79,79,79,79,79,79,6d,6d,6d,6d,6d,
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endmodule
