// Digital circuit 74189_RAM_upper.dig as structural Verilog
// 64-Bit Random Access Memory with 3-STATE Outputs
module _74189_RAM_upper (
  input  A0,
  input  A1,
  input  A2,
  input  A3,
  input  D0,
  input  D1,
  input  D2,
  input  D3,
  input  nCS,
  input  nWE,
  input  VCC,
  input  GND,
  output Q0,
  output Q1,
  output Q2,
  output Q3
);

  wire and_1_out, and_2_out;
  wire [3:0] not_1_out, ramdualport_d;

  and and_1 (and_1_out, ~nWE, ~nCS);  // And
  and and_2 (and_2_out, nWE, ~nCS);  // And
  RAMDualPort #(.AddrBits(4), .isProgramMemory("true"), .Bits(4)) ramdualport (
    .A({A3, A2, A1, A0}), .Din({D3, D2, D1, D0}), .str(and_1_out), .C(and_1_out), .ld(and_2_out),
    .D(ramdualport_d));
  assign not_1_out = ~ramdualport_d;  // Not not_1, 4 bits wide
  assign {Q3, Q2, Q1, Q0} = and_2_out ? not_1_out : 4'bz;  // Driver driver_1
  PowerSupply powersupply_1 (.VDD(VCC), .GND(GND));

  // Notes on the sheet:
  //   A0: pin 1
  //   A1: pin 15
  //   A2: pin 14
  //   A3: pin 13
  //   D0: pin 4
  //   D1: pin 6
  //   D2: pin 10
  //   D3: pin 12
  //   Q0: pin 5
  //   Q1: pin 7
  //   Q2: pin 9
  //   Q3: pin 11
  //   nCS: pin 2, default 1
  //   nWE: pin 3, default 1
  //   VCC: pin 16, default 1
  //   GND: pin 8
endmodule
