// Digital circuit ALU.dig as structural Verilog
module ALU (
  input  CLK,
  input  EO,
  input  [7:0] B_in,
  input  SU,
  input  CLR,
  input  FI,
  input  [7:0] A_in,
  output CF,
  output ZF,
  output [7:0] BUS
);

  wire bussplitter_1_d0, bussplitter_1_d1, bussplitter_1_d2, bussplitter_1_d3, bussplitter_1_d4,
       bussplitter_1_d5, bussplitter_1_d6, bussplitter_1_d7, notconnected_1_out, notconnected_2_out,
       U19__Register_pin14, U20__Adder_MSB_pin2, U20__Adder_MSB_pin6, U20__Adder_MSB_pin7,
       U20__Adder_MSB_pin11, U20__Adder_MSB_pin15, U21__Adder_LSB_pin2, U21__Adder_LSB_pin6,
       U21__Adder_LSB_pin11, U21__Adder_LSB_pin15, U22__NOR_pin2, U22__NOR_pin3, U22__NOR_pin5,
       U22__NOR_pin6, U22__NOR_pin8, U22__NOR_pin9, U22__NOR_pin11, U22__NOR_pin12, U23__AND_pin1,
       U23__AND_pin2, U23__AND_pin3, U23__AND_pin4, U23__AND_pin5, U23__AND_pin6, U23__AND_pin11;

  // NotConnected on notconnected_1_out
  _7408 U23__AND (
    .pin1(U23__AND_pin1), .pin2(U23__AND_pin2), .pin3(U23__AND_pin3), .pin4(U23__AND_pin4),
    .pin5(U23__AND_pin5), .pin6(U23__AND_pin6), .pin7(1'b0), .pin9(1'b1), .pin10(1'b1),
    .pin11(U23__AND_pin11), .pin12(U23__AND_pin6), .pin13(U23__AND_pin3), .pin14(1'b1));  // open: pin8
  // NotConnected on notconnected_2_out
  LED u_CF (.in(CF));
  LED u_ZF (.in(ZF));
  _74173 U19__Register (
    .pin1(1'b0), .pin2(1'b0), .pin3(CF), .pin4(ZF), .pin7(CLK), .pin8(1'b0), .pin9(FI), .pin10(FI),
    .pin11(notconnected_1_out), .pin12(notconnected_2_out), .pin13(U23__AND_pin11),
    .pin14(U19__Register_pin14), .pin15(CLR), .pin16(1'b1));  // open: pin5, pin6
  _7402 U22__NOR (
    .pin1(U23__AND_pin4), .pin2(U22__NOR_pin2), .pin3(U22__NOR_pin3), .pin4(U23__AND_pin5),
    .pin5(U22__NOR_pin5), .pin6(U22__NOR_pin6), .pin7(1'b0), .pin8(U22__NOR_pin8), .pin9(U22__NOR_pin9),
    .pin10(U23__AND_pin1), .pin11(U22__NOR_pin11), .pin12(U22__NOR_pin12), .pin13(U23__AND_pin2), .pin14(1'b1));
  BusSplitter #(.Bits(8)) bussplitter_1 (
    .D(BUS), .OE(EO), .D0(bussplitter_1_d0), .D1(bussplitter_1_d1), .D2(bussplitter_1_d2),
    .D3(bussplitter_1_d3), .D4(bussplitter_1_d4), .D5(bussplitter_1_d5), .D6(bussplitter_1_d6),
    .D7(bussplitter_1_d7));
  _74245 U17_3st_Xceiver (
    .pin1(1'b1), .pin2(U22__NOR_pin6), .pin3(U22__NOR_pin5), .pin4(U22__NOR_pin3), .pin5(U22__NOR_pin2),
    .pin6(U22__NOR_pin12), .pin7(U22__NOR_pin11), .pin8(U22__NOR_pin9), .pin9(U22__NOR_pin8), .pin10(1'b0),
    .pin11(bussplitter_1_d0), .pin12(bussplitter_1_d1), .pin13(bussplitter_1_d2), .pin14(bussplitter_1_d3),
    .pin15(bussplitter_1_d4), .pin16(bussplitter_1_d5), .pin17(bussplitter_1_d6), .pin18(bussplitter_1_d7),
    .pin19(EO), .pin20(1'b1));
  LED led_1 (.in(U22__NOR_pin6));
  LED led_2 (.in(U22__NOR_pin5));
  LED led_3 (.in(U22__NOR_pin3));
  LED led_4 (.in(U22__NOR_pin2));
  LED led_5 (.in(U22__NOR_pin12));
  LED led_6 (.in(U22__NOR_pin11));
  LED led_7 (.in(U22__NOR_pin9));
  LED led_8 (.in(U22__NOR_pin8));
  _74283 U20__Adder_MSB (
    .pin1(U22__NOR_pin3), .pin2(U20__Adder_MSB_pin2), .pin3(A_in[5]), .pin4(U22__NOR_pin2), .pin5(A_in[4]),
    .pin6(U20__Adder_MSB_pin6), .pin7(U20__Adder_MSB_pin7), .pin8(1'b0), .pin9(U19__Register_pin14),
    .pin10(U22__NOR_pin6), .pin11(U20__Adder_MSB_pin11), .pin12(A_in[7]), .pin13(U22__NOR_pin5),
    .pin14(A_in[6]), .pin15(U20__Adder_MSB_pin15), .pin16(1'b1));
  _74283 U21__Adder_LSB (
    .pin1(U22__NOR_pin9), .pin2(U21__Adder_LSB_pin2), .pin3(A_in[1]), .pin4(U22__NOR_pin8), .pin5(A_in[0]),
    .pin6(U21__Adder_LSB_pin6), .pin7(SU), .pin8(1'b0), .pin9(U20__Adder_MSB_pin7), .pin10(U22__NOR_pin12),
    .pin11(U21__Adder_LSB_pin11), .pin12(A_in[3]), .pin13(U22__NOR_pin11), .pin14(A_in[2]),
    .pin15(U21__Adder_LSB_pin15), .pin16(1'b1));
  _7486 U16__XOR (
    .pin1(B_in[7]), .pin2(SU), .pin3(U20__Adder_MSB_pin11), .pin4(B_in[6]), .pin5(SU),
    .pin6(U20__Adder_MSB_pin15), .pin7(1'b0), .pin8(U20__Adder_MSB_pin2), .pin9(B_in[5]), .pin10(SU),
    .pin11(U20__Adder_MSB_pin6), .pin12(B_in[4]), .pin13(SU), .pin14(1'b1));
  _7486 U18__XOR (
    .pin1(B_in[3]), .pin2(SU), .pin3(U21__Adder_LSB_pin11), .pin4(B_in[2]), .pin5(SU),
    .pin6(U21__Adder_LSB_pin15), .pin7(1'b0), .pin8(U21__Adder_LSB_pin2), .pin9(B_in[1]), .pin10(SU),
    .pin11(U21__Adder_LSB_pin6), .pin12(B_in[0]), .pin13(SU), .pin14(1'b1));
  // Pins of 1 and 8 bits meet at BUS

  // Notes on the sheet:
  //   EO: default 1
  //   FI: default 1
endmodule
