// Digital circuit SAP-1.dig as structural Verilog
module SAP_1 (
  input  clk,
  input  Refresh_display
);

  wire _7400_1_pin1, _7400_1_pin3, _7400_1_pin4, _7400_1_pin12, _7404_1_pin1, _7404_1_pin3, _7404_1_pin5,
       _7404_1_pin9, _7404_1_pin11, _7404_1_pin13, _7404_2_pin1, _7404_2_pin3, _7404_2_pin5, _7404_2_pin9,
       _7404_2_pin11, _7404_3_pin1, _7404_3_pin3, _7404_3_pin5, _7404_3_pin9, _7404_4_pin1, _7404_4_pin3,
       _7404_4_pin5, _7404_4_pin9, _7476_1_pin6, _7476_1_pin10, _74138_1_pin11, _74138_1_pin12,
       _74138_1_pin13, _74138_1_pin14, _74138_1_pin15, _74139_1_pin4, _74139_1_pin5, _74139_1_pin6,
       _74139_1_pin7, _74157_1_pin12, _74157_1_pin13, _74157_1_pin14, _74161_1_pin3, _74161_1_pin12,
       _74161_1_pin13, _74161_1_pin14, _74161_2_pin11, _74161_2_pin12, _74161_2_pin13, _74161_2_pin14,
       _74189_1_pin4, _74189_1_pin6, _74189_1_pin10, _74189_1_pin12, _74189_2_pin4, _74189_2_pin6,
       _74189_2_pin10, _74189_2_pin12, _74245_2_pin2, _74245_2_pin3, _74245_2_pin4, _74245_2_pin5,
       _74245_2_pin6, _74245_2_pin7, _74245_2_pin8, _74245_2_pin9, _74245_2_pin11, _74245_2_pin12,
       _74245_2_pin13, _74245_2_pin14, _74245_2_pin15, _74245_2_pin16, _74245_2_pin17, _74245_2_pin18,
       _74273_1_pin2, _74273_1_pin5, _74273_1_pin6, _74273_1_pin9, _74273_1_pin11, _74273_1_pin12,
       _74273_1_pin15, _74273_1_pin16, _74273_1_pin19, AI, AO, BI, Burn_out, bussplitter_3_d0,
       bussplitter_3_d1, bussplitter_3_d2, bussplitter_3_d3, bussplitter_3_d4, bussplitter_3_d5,
       bussplitter_3_d6, bussplitter_3_d7, bussplitter_4_d0, bussplitter_4_d1, bussplitter_4_d2,
       bussplitter_4_d3, bussplitter_4_d4, bussplitter_4_d5, bussplitter_4_d6, bussplitter_4_d7, CE, CF,
       CLK_t, CLK_t_t, CLR, CLR_t, CO, dipswitch_1_out, EO, FI, HALT, II, IO, J, MI, not_1_out, not_4_out,
       OI, or_1_out, PROG_EN_out, RI, RO, STEP_2_out, STEP_out, SU, U5_AND_pin4, U5_AND_pin9, U6_OR_pin1,
       U6_OR_pin2, U6_OR_pin3, U8__Reg_Upper_2_pin11, U8__Reg_Upper_2_pin12, U8__Reg_Upper_2_pin13,
       U8__Reg_Upper_2_pin14, U8__Reg_Upper_3_pin3, U8__Reg_Upper_3_pin4, U8__Reg_Upper_3_pin5,
       U8__Reg_Upper_3_pin6, U8__Reg_Upper_3_pin11, U8__Reg_Upper_3_pin12, U8__Reg_Upper_3_pin13,
       U8__Reg_Upper_3_pin14, U9__Reg_Lower_2_pin11, U9__Reg_Lower_2_pin12, U9__Reg_Lower_2_pin13,
       U9__Reg_Lower_2_pin14, U9__Reg_Lower_3_pin3, U9__Reg_Lower_3_pin4, U9__Reg_Lower_3_pin5,
       U9__Reg_Lower_3_pin6, U9__Reg_Lower_3_pin11, U9__Reg_Lower_3_pin12, U9__Reg_Lower_3_pin13,
       U9__Reg_Lower_3_pin14, U16__XOR_pin3, U16__XOR_pin6, U16__XOR_pin8, U16__XOR_pin11, U18__XOR_pin3,
       U18__XOR_pin6, U18__XOR_pin8, U18__XOR_pin11, U19__Register_pin11, U19__Register_pin12,
       U19__Register_pin13, U20__Adder_MSB_pin1, U20__Adder_MSB_pin4, U20__Adder_MSB_pin9,
       U20__Adder_MSB_pin10, U20__Adder_MSB_pin13, U21__Adder_LSB_pin1, U21__Adder_LSB_pin4,
       U21__Adder_LSB_pin9, U21__Adder_LSB_pin10, U21__Adder_LSB_pin13, U22__NOR_pin1, U22__NOR_pin4,
       U22__NOR_pin10, U22__NOR_pin13, U23__AND_pin3, U23__AND_pin6, U33__2bit_Mux_pin1, U33__2bit_Mux_pin3,
       U33__2bit_Mux_pin4, U33__2bit_Mux_pin6, U33__2bit_Mux_pin7, U33__2bit_Mux_pin9, U33__2bit_Mux_pin10,
       U33__2bit_Mux_pin12, U33__2bit_Mux_pin13, undriven, undriven_2, undriven_3, undriven_4, undriven_5,
       undriven_6, undriven_7, undriven_8, ZF;
  wire [3:0] U33__2bit_Mux_pin14;
  wire [7:0] dipswitch_6_out, driver_1_out, U8__Reg_Upper_pin13, U9__Reg_Lower_2_pin6, U9__Reg_Lower_pin6;

  _7400 _7400_1 (
    .pin1(_7400_1_pin1), .pin2(_7400_1_pin1), .pin3(_7400_1_pin3), .pin4(_7400_1_pin4), .pin5(CLR),
    .pin6(_7400_1_pin1), .pin7(1'b0), .pin8(CLR_t), .pin9(CLR), .pin10(CLR), .pin11(CLR),
    .pin12(_7400_1_pin12), .pin13(_7400_1_pin12), .pin14(1'b1));
  Button button_1 (.out(_7400_1_pin12));
  LED T_1 (.in(_74138_1_pin15));
  LED T_2 (.in(_74138_1_pin14));
  LED T_3 (.in(_74138_1_pin13));
  LED T_4 (.in(_74138_1_pin12));
  LED T_5 (.in(_74138_1_pin11));
  _74161 _74161_1 (
    .pin1(_7400_1_pin3), .pin2(CLK_t), .pin3(_74161_1_pin3), .pin4(_74161_1_pin3), .pin5(_74161_1_pin3),
    .pin6(_74161_1_pin3), .pin7(1'b1), .pin8(1'b0), .pin9(1'b1), .pin10(1'b1), .pin12(_74161_1_pin12),
    .pin13(_74161_1_pin13), .pin14(_74161_1_pin14), .pin16(1'b1));  // open: pin11, pin15
  // NotConnected on _74161_1_pin3
  _74138 _74138_1 (
    .pin1(_74161_1_pin14), .pin2(_74161_1_pin13), .pin3(_74161_1_pin12), .pin4(1'b0), .pin5(1'b0),
    .pin6(1'b1), .pin8(1'b0), .pin10(_7400_1_pin4), .pin11(_74138_1_pin11), .pin12(_74138_1_pin12),
    .pin13(_74138_1_pin13), .pin14(_74138_1_pin14), .pin15(_74138_1_pin15), .pin16(1'b1));  // open: pin7, pin9
  _28c16_ucode_upper _28c16_ucode_upper_1 (
    .A0(_74161_1_pin14), .A1(_74161_1_pin13), .A2(_74161_1_pin12), .A3(U8__Reg_Upper_3_pin6),
    .A4(U8__Reg_Upper_3_pin5), .A5(U8__Reg_Upper_3_pin4), .A6(U8__Reg_Upper_3_pin3), .A7(1'b0), .A8(CF),
    .A9(ZF), .A10(1'b0), .nCE(1'b0), .nOE(1'b0), .nWE(1'b1), .VCC(1'b1), .GND(1'b0), .I_O0(_7404_1_pin13),
    .I_O1(_7404_1_pin11), .I_O2(_7404_1_pin9), .I_O3(_7404_1_pin5), .I_O4(_7404_1_pin3), .I_O5(RI),
    .I_O6(_7404_1_pin1), .I_O7(HALT));
  _28c16_ucode_lower _28c16_ucode_lower_1 (
    .A0(_74161_1_pin14), .A1(_74161_1_pin13), .A2(_74161_1_pin12), .A3(U8__Reg_Upper_3_pin6),
    .A4(U8__Reg_Upper_3_pin5), .A5(U8__Reg_Upper_3_pin4), .A6(U8__Reg_Upper_3_pin3), .A7(1'b0), .A8(CF),
    .A9(ZF), .A10(1'b0), .nCE(1'b0), .nOE(1'b0), .nWE(1'b1), .VCC(1'b1), .GND(1'b0), .I_O0(_7404_2_pin11),
    .I_O1(_7404_2_pin9), .I_O2(_7404_2_pin5), .I_O3(CE), .I_O4(OI), .I_O5(_7404_2_pin3), .I_O6(SU),
    .I_O7(_7404_2_pin1));
  _74173 U9__Reg_Lower (
    .pin1(1'b0), .pin2(1'b0), .pin3(U9__Reg_Lower_pin6[3]), .pin4(U9__Reg_Lower_pin6[2]),
    .pin5(U9__Reg_Lower_pin6[1]), .pin6(U9__Reg_Lower_pin6[0]), .pin7(CLK_t_t), .pin8(1'b0), .pin9(BI),
    .pin10(BI), .pin11(U8__Reg_Upper_pin13[0]), .pin12(U8__Reg_Upper_pin13[1]),
    .pin13(U8__Reg_Upper_pin13[2]), .pin14(U8__Reg_Upper_pin13[3]), .pin15(CLR_t), .pin16(1'b1));
  DipSwitch STEP (.out(STEP_out));
  Button STEP_2 (.out(STEP_2_out));
  _7432 U6_OR (
    .pin1(U6_OR_pin1), .pin2(U6_OR_pin2), .pin3(U6_OR_pin3), .pin4(1'b0), .pin5(1'b0), .pin7(1'b0),
    .pin9(1'b1), .pin10(1'b1), .pin12(1'b1), .pin13(1'b1), .pin14(1'b1));  // open: pin6, pin8, pin11
  _74173 U9__Reg_Lower_2 (
    .pin1(1'b0), .pin2(1'b0), .pin3(U9__Reg_Lower_2_pin6[3]), .pin4(U9__Reg_Lower_2_pin6[2]),
    .pin5(U9__Reg_Lower_2_pin6[1]), .pin6(U9__Reg_Lower_2_pin6[0]), .pin7(CLK_t_t), .pin8(1'b0), .pin9(AI),
    .pin10(AI), .pin11(U9__Reg_Lower_2_pin11), .pin12(U9__Reg_Lower_2_pin12), .pin13(U9__Reg_Lower_2_pin13),
    .pin14(U9__Reg_Lower_2_pin14), .pin15(CLR_t), .pin16(1'b1));
  _74173 U9__Reg_Lower_3 (
    .pin1(1'b0), .pin2(1'b0), .pin3(U9__Reg_Lower_3_pin3), .pin4(U9__Reg_Lower_3_pin4),
    .pin5(U9__Reg_Lower_3_pin5), .pin6(U9__Reg_Lower_3_pin6), .pin7(CLK_t_t), .pin8(1'b0), .pin9(II),
    .pin10(II), .pin11(U9__Reg_Lower_3_pin11), .pin12(U9__Reg_Lower_3_pin12), .pin13(U9__Reg_Lower_3_pin13),
    .pin14(U9__Reg_Lower_3_pin14), .pin15(CLR_t), .pin16(1'b1));
  _7408 U5_AND (
    .pin1(clk), .pin2(STEP_out), .pin3(U6_OR_pin1), .pin4(U5_AND_pin4), .pin5(STEP_2_out), .pin6(U6_OR_pin2),
    .pin7(1'b0), .pin8(CLK_t_t), .pin9(U5_AND_pin9), .pin10(U6_OR_pin3), .pin12(1'b1), .pin13(1'b1),
    .pin14(1'b1));  // open: pin11
  _7404 U4_NOT (
    .pin1(STEP_out), .pin2(U5_AND_pin4), .pin3(1'b0), .pin5(1'b0), .pin7(1'b0), .pin8(U5_AND_pin9),
    .pin9(HALT), .pin11(1'b1), .pin12(CLK_t), .pin13(CLK_t_t), .pin14(1'b1));  // open: pin4, pin6, pin10
  LED u_CLK (.in(CLK_t_t));
  _74173 U8__Reg_Upper (
    .pin1(1'b0), .pin2(1'b0), .pin3(U9__Reg_Lower_pin6[7]), .pin4(U9__Reg_Lower_pin6[6]),
    .pin5(U9__Reg_Lower_pin6[5]), .pin6(U9__Reg_Lower_pin6[4]), .pin7(CLK_t_t), .pin8(1'b0), .pin9(BI),
    .pin10(BI), .pin11(U8__Reg_Upper_pin13[4]), .pin12(U8__Reg_Upper_pin13[5]),
    .pin13(U8__Reg_Upper_pin13[6]), .pin14(U8__Reg_Upper_pin13[7]), .pin15(CLR_t), .pin16(1'b1));
  _74173 U8__Reg_Upper_2 (
    .pin1(1'b0), .pin2(1'b0), .pin3(U9__Reg_Lower_2_pin6[7]), .pin4(U9__Reg_Lower_2_pin6[6]),
    .pin5(U9__Reg_Lower_2_pin6[5]), .pin6(U9__Reg_Lower_2_pin6[4]), .pin7(CLK_t_t), .pin8(1'b0), .pin9(AI),
    .pin10(AI), .pin11(U8__Reg_Upper_2_pin11), .pin12(U8__Reg_Upper_2_pin12), .pin13(U8__Reg_Upper_2_pin13),
    .pin14(U8__Reg_Upper_2_pin14), .pin15(CLR_t), .pin16(1'b1));
  LED led_1 (.in(U9__Reg_Lower_pin6[0]));
  _7404 _7404_1 (
    .pin1(_7404_1_pin1), .pin2(MI), .pin3(_7404_1_pin3), .pin4(RO), .pin5(_7404_1_pin5), .pin6(IO),
    .pin7(1'b0), .pin8(II), .pin9(_7404_1_pin9), .pin10(AI), .pin11(_7404_1_pin11), .pin12(AO),
    .pin13(_7404_1_pin13), .pin14(1'b1));
  _7404 _7404_2 (
    .pin1(_7404_2_pin1), .pin2(EO), .pin3(_7404_2_pin3), .pin4(BI), .pin5(_7404_2_pin5), .pin6(CO),
    .pin7(1'b0), .pin8(J), .pin9(_7404_2_pin9), .pin10(FI), .pin11(_7404_2_pin11), .pin13(1'b1), .pin14(1'b1));  // open: pin12
  _74173 U8__Reg_Upper_3 (
    .pin1(1'b0), .pin2(1'b0), .pin3(U8__Reg_Upper_3_pin3), .pin4(U8__Reg_Upper_3_pin4),
    .pin5(U8__Reg_Upper_3_pin5), .pin6(U8__Reg_Upper_3_pin6), .pin7(CLK_t_t), .pin8(1'b0), .pin9(II),
    .pin10(II), .pin11(U8__Reg_Upper_3_pin11), .pin12(U8__Reg_Upper_3_pin12), .pin13(U8__Reg_Upper_3_pin13),
    .pin14(U8__Reg_Upper_3_pin14), .pin15(CLR_t), .pin16(1'b1));
  LED led_2 (.in(U9__Reg_Lower_pin6[2]));
  LED led_3 (.in(U9__Reg_Lower_pin6[1]));
  LED led_4 (.in(U9__Reg_Lower_2_pin6[1]));
  LED led_5 (.in(U9__Reg_Lower_2_pin6[0]));
  LED led_6 (.in(U9__Reg_Lower_pin6[4]));
  LED led_7 (.in(U9__Reg_Lower_pin6[3]));
  LED led_8 (.in(U9__Reg_Lower_2_pin6[3]));
  LED led_9 (.in(U9__Reg_Lower_2_pin6[2]));
  LED led_10 (.in(U9__Reg_Lower_pin6[6]));
  LED led_11 (.in(U9__Reg_Lower_pin6[5]));
  LED led_12 (.in(U8__Reg_Upper_3_pin3));
  LED led_13 (.in(U9__Reg_Lower_2_pin6[5]));
  LED led_14 (.in(U9__Reg_Lower_2_pin6[4]));
  LED led_15 (.in(U9__Reg_Lower_pin6[7]));
  _74245 U7_3st_Xceiver (
    .pin1(1'b1), .pin2(U9__Reg_Lower_pin6[7]), .pin3(U9__Reg_Lower_pin6[6]), .pin4(U9__Reg_Lower_pin6[5]),
    .pin5(U9__Reg_Lower_pin6[4]), .pin6(U9__Reg_Lower_pin6[3]), .pin7(U9__Reg_Lower_pin6[2]),
    .pin8(U9__Reg_Lower_pin6[1]), .pin9(U9__Reg_Lower_pin6[0]), .pin10(1'b0), .pin11(U8__Reg_Upper_pin13[0]),
    .pin12(U8__Reg_Upper_pin13[1]), .pin13(U8__Reg_Upper_pin13[2]), .pin14(U8__Reg_Upper_pin13[3]),
    .pin15(U8__Reg_Upper_pin13[4]), .pin16(U8__Reg_Upper_pin13[5]), .pin17(U8__Reg_Upper_pin13[6]),
    .pin18(U8__Reg_Upper_pin13[7]), .pin19(1'b1), .pin20(1'b1));
  LED led_16 (.in(U8__Reg_Upper_3_pin5));
  LED led_17 (.in(U8__Reg_Upper_3_pin4));
  LED led_18 (.in(U9__Reg_Lower_2_pin6[7]));
  LED led_19 (.in(U9__Reg_Lower_2_pin6[6]));
  BusSplitter #(.Bits(8)) bussplitter_1 (
    .D(U8__Reg_Upper_pin13), .OE(AO), .D0(U9__Reg_Lower_2_pin11), .D1(U9__Reg_Lower_2_pin12),
    .D2(U9__Reg_Lower_2_pin13), .D3(U9__Reg_Lower_2_pin14), .D4(U8__Reg_Upper_2_pin11),
    .D5(U8__Reg_Upper_2_pin12), .D6(U8__Reg_Upper_2_pin13), .D7(U8__Reg_Upper_2_pin14));
  LED led_20 (.in(U8__Reg_Upper_3_pin6));
  _74245 U7_3st_Xceiver_2 (
    .pin1(1'b1), .pin2(U8__Reg_Upper_3_pin6), .pin3(U8__Reg_Upper_3_pin5), .pin4(U8__Reg_Upper_3_pin4),
    .pin5(U8__Reg_Upper_3_pin3), .pin6(U9__Reg_Lower_3_pin6), .pin7(U9__Reg_Lower_3_pin5),
    .pin8(U9__Reg_Lower_3_pin4), .pin9(U9__Reg_Lower_3_pin3), .pin10(1'b0), .pin11(U9__Reg_Lower_3_pin14),
    .pin12(U9__Reg_Lower_3_pin13), .pin13(U9__Reg_Lower_3_pin12), .pin14(U9__Reg_Lower_3_pin11),
    .pin15(U8__Reg_Upper_3_pin14), .pin16(U8__Reg_Upper_3_pin13), .pin17(U8__Reg_Upper_3_pin12),
    .pin18(U8__Reg_Upper_3_pin11), .pin19(IO), .pin20(1'b1));
  BusSplitter #(.Bits(8)) bussplitter_2 (
    .D(U8__Reg_Upper_pin13), .OE(IO), .D0(U9__Reg_Lower_3_pin11), .D1(U9__Reg_Lower_3_pin12),
    .D2(U9__Reg_Lower_3_pin13), .D3(U9__Reg_Lower_3_pin14), .D4(U8__Reg_Upper_3_pin11),
    .D5(U8__Reg_Upper_3_pin12), .D6(U8__Reg_Upper_3_pin13), .D7(U8__Reg_Upper_3_pin14));
  _74245 U7_3st_Xceiver_3 (
    .pin1(1'b1), .pin2(U9__Reg_Lower_2_pin6[7]), .pin3(U9__Reg_Lower_2_pin6[6]),
    .pin4(U9__Reg_Lower_2_pin6[5]), .pin5(U9__Reg_Lower_2_pin6[4]), .pin6(U9__Reg_Lower_2_pin6[3]),
    .pin7(U9__Reg_Lower_2_pin6[2]), .pin8(U9__Reg_Lower_2_pin6[1]), .pin9(U9__Reg_Lower_2_pin6[0]),
    .pin10(1'b0), .pin11(U9__Reg_Lower_2_pin11), .pin12(U9__Reg_Lower_2_pin12),
    .pin13(U9__Reg_Lower_2_pin13), .pin14(U9__Reg_Lower_2_pin14), .pin15(U8__Reg_Upper_2_pin11),
    .pin16(U8__Reg_Upper_2_pin12), .pin17(U8__Reg_Upper_2_pin13), .pin18(U8__Reg_Upper_2_pin14), .pin19(AO),
    .pin20(1'b1));
  BusSplitter #(.Bits(8)) bussplitter_3 (
    .D(U8__Reg_Upper_pin13), .OE(CO), .D0(bussplitter_3_d0), .D1(bussplitter_3_d1), .D2(bussplitter_3_d2),
    .D3(bussplitter_3_d3), .D4(bussplitter_3_d4), .D5(bussplitter_3_d5), .D6(bussplitter_3_d6),
    .D7(bussplitter_3_d7));
  _28c16_DisplayOut _28c16_displayout_1 (
    .A0(_74273_1_pin2), .A1(_74273_1_pin5), .A2(_74273_1_pin6), .A3(_74273_1_pin9), .A4(_74273_1_pin12),
    .A5(_74273_1_pin15), .A6(_74273_1_pin16), .A7(_74273_1_pin19), .A8(_7476_1_pin6), .A9(_7476_1_pin10),
    .A10(dipswitch_1_out), .nCE(1'b0), .nOE(1'b0), .nWE(1'b1), .VCC(1'b1), .GND(1'b0), .I_O0(undriven_7),
    .I_O1(undriven_2), .I_O2(undriven_4), .I_O3(undriven_6), .I_O4(undriven_5), .I_O5(undriven_3),
    .I_O6(undriven), .I_O7(undriven_8));
  _74273 _74273_1 (
    .pin1(CLR), .pin2(_74273_1_pin2), .pin3(U8__Reg_Upper_pin13[0]), .pin4(U8__Reg_Upper_pin13[1]),
    .pin5(_74273_1_pin5), .pin6(_74273_1_pin6), .pin7(U8__Reg_Upper_pin13[2]), .pin8(U8__Reg_Upper_pin13[3]),
    .pin9(_74273_1_pin9), .pin10(1'b0), .pin11(_74273_1_pin11), .pin12(_74273_1_pin12),
    .pin13(U8__Reg_Upper_pin13[4]), .pin14(U8__Reg_Upper_pin13[5]), .pin15(_74273_1_pin15),
    .pin16(_74273_1_pin16), .pin17(U8__Reg_Upper_pin13[6]), .pin18(U8__Reg_Upper_pin13[7]),
    .pin19(_74273_1_pin19), .pin20(1'b1));
  _74161 _74161_2 (
    .pin1(CLR), .pin2(CLK_t_t), .pin3(bussplitter_3_d0), .pin4(bussplitter_3_d1), .pin5(bussplitter_3_d2),
    .pin6(bussplitter_3_d3), .pin7(CE), .pin8(1'b0), .pin9(J), .pin10(CE), .pin11(_74161_2_pin11),
    .pin12(_74161_2_pin12), .pin13(_74161_2_pin13), .pin14(_74161_2_pin14), .pin16(1'b1));  // open: pin15
  DipSwitch dipswitch_1 (.out(dipswitch_1_out));
  _7486 U18__XOR (
    .pin1(U9__Reg_Lower_pin6[3]), .pin2(SU), .pin3(U18__XOR_pin3), .pin4(U9__Reg_Lower_pin6[2]), .pin5(SU),
    .pin6(U18__XOR_pin6), .pin7(1'b0), .pin8(U18__XOR_pin8), .pin9(U9__Reg_Lower_pin6[1]), .pin10(SU),
    .pin11(U18__XOR_pin11), .pin12(U9__Reg_Lower_pin6[0]), .pin13(SU), .pin14(1'b1));
  _7486 U16__XOR (
    .pin1(U9__Reg_Lower_pin6[7]), .pin2(SU), .pin3(U16__XOR_pin3), .pin4(U9__Reg_Lower_pin6[6]), .pin5(SU),
    .pin6(U16__XOR_pin6), .pin7(1'b0), .pin8(U16__XOR_pin8), .pin9(U9__Reg_Lower_pin6[5]), .pin10(SU),
    .pin11(U16__XOR_pin11), .pin12(U9__Reg_Lower_pin6[4]), .pin13(SU), .pin14(1'b1));
  _7408 _7408_1 (
    .pin1(CLK_t_t), .pin2(OI), .pin3(_74273_1_pin11), .pin4(1'b0), .pin5(1'b0), .pin7(1'b0), .pin9(1'b1),
    .pin10(1'b1), .pin12(1'b1), .pin13(1'b1), .pin14(1'b1));  // open: pin6, pin8, pin11
  _7476 _7476_1 (
    .pin1(Refresh_display), .pin2(1'b1), .pin3(1'b1), .pin4(1'b1), .pin5(1'b1), .pin6(_7476_1_pin6),
    .pin7(1'b1), .pin8(1'b1), .pin9(1'b1), .pin10(_7476_1_pin10), .pin12(1'b1), .pin13(1'b0),
    .pin14(_7476_1_pin6), .pin16(1'b1));  // open: pin11, pin15
  LED led_21 (.in(_74161_2_pin11));
  LED led_22 (.in(_74161_2_pin12));
  LED led_23 (.in(_74161_2_pin13));
  Seven_Seg #(.commonCathode("true")) seven_seg_1 (
    .a(undriven), .b(undriven_3), .c(undriven_5), .d(undriven_6), .e(undriven_4), .f(undriven_2),
    .g(undriven_7), .dp(undriven_8), .common(_74139_1_pin7));
  LED led_24 (.in(_74161_2_pin14));
  _74283 U21__Adder_LSB (
    .pin1(U21__Adder_LSB_pin1), .pin2(U18__XOR_pin8), .pin3(U9__Reg_Lower_2_pin6[1]),
    .pin4(U21__Adder_LSB_pin4), .pin5(U9__Reg_Lower_2_pin6[0]), .pin6(U18__XOR_pin11), .pin7(SU),
    .pin8(1'b0), .pin9(U21__Adder_LSB_pin9), .pin10(U21__Adder_LSB_pin10), .pin11(U18__XOR_pin3),
    .pin12(U9__Reg_Lower_2_pin6[3]), .pin13(U21__Adder_LSB_pin13), .pin14(U9__Reg_Lower_2_pin6[2]),
    .pin15(U18__XOR_pin6), .pin16(1'b1));
  _74283 U20__Adder_MSB (
    .pin1(U20__Adder_MSB_pin1), .pin2(U16__XOR_pin8), .pin3(U9__Reg_Lower_2_pin6[5]),
    .pin4(U20__Adder_MSB_pin4), .pin5(U9__Reg_Lower_2_pin6[4]), .pin6(U16__XOR_pin11),
    .pin7(U21__Adder_LSB_pin9), .pin8(1'b0), .pin9(U20__Adder_MSB_pin9), .pin10(U20__Adder_MSB_pin10),
    .pin11(U16__XOR_pin3), .pin12(U9__Reg_Lower_2_pin6[7]), .pin13(U20__Adder_MSB_pin13),
    .pin14(U9__Reg_Lower_2_pin6[6]), .pin15(U16__XOR_pin6), .pin16(1'b1));
  _74139 _74139_1 (
    .pin1(1'b0), .pin2(_7476_1_pin6), .pin3(_7476_1_pin10), .pin4(_74139_1_pin4), .pin5(_74139_1_pin5),
    .pin6(_74139_1_pin6), .pin7(_74139_1_pin7), .pin8(1'b0), .pin13(1'b1), .pin14(1'b1), .pin15(1'b1),
    .pin16(1'b1));  // open: pin9, pin10, pin11, pin12
  Seven_Seg #(.commonCathode("true")) seven_seg_2 (
    .a(undriven), .b(undriven_3), .c(undriven_5), .d(undriven_6), .e(undriven_4), .f(undriven_2),
    .g(undriven_7), .dp(undriven_8), .common(_74139_1_pin6));
  _74245 _74245_1 (
    .pin1(1'b1), .pin2(1'b0), .pin3(1'b0), .pin4(1'b0), .pin5(1'b0), .pin6(_74161_2_pin14),
    .pin7(_74161_2_pin13), .pin8(_74161_2_pin12), .pin9(_74161_2_pin11), .pin10(1'b0),
    .pin11(bussplitter_3_d3), .pin12(bussplitter_3_d2), .pin13(bussplitter_3_d1), .pin14(bussplitter_3_d0),
    .pin15(bussplitter_3_d4), .pin16(bussplitter_3_d5), .pin17(bussplitter_3_d6), .pin18(bussplitter_3_d7),
    .pin19(CO), .pin20(1'b1));
  Seven_Seg #(.commonCathode("true")) seven_seg_3 (
    .a(undriven), .b(undriven_3), .c(undriven_5), .d(undriven_6), .e(undriven_4), .f(undriven_2),
    .g(undriven_7), .dp(undriven_8), .common(_74139_1_pin5));
  BusSplitter #(.Bits(8)) bussplitter_4 (
    .D(U8__Reg_Upper_pin13), .OE(EO), .D0(bussplitter_4_d0), .D1(bussplitter_4_d1), .D2(bussplitter_4_d2),
    .D3(bussplitter_4_d3), .D4(bussplitter_4_d4), .D5(bussplitter_4_d5), .D6(bussplitter_4_d6),
    .D7(bussplitter_4_d7));
  LED led_25 (.in(U21__Adder_LSB_pin1));
  LED led_26 (.in(U21__Adder_LSB_pin4));
  Seven_Seg #(.commonCathode("true")) seven_seg_4 (
    .a(undriven), .b(undriven_3), .c(undriven_5), .d(undriven_6), .e(undriven_4), .f(undriven_2),
    .g(undriven_7), .dp(undriven_8), .common(_74139_1_pin4));
  LED led_27 (.in(U21__Adder_LSB_pin10));
  LED led_28 (.in(U21__Adder_LSB_pin13));
  LED led_29 (.in(U20__Adder_MSB_pin1));
  LED led_30 (.in(U20__Adder_MSB_pin4));
  LED led_31 (.in(U20__Adder_MSB_pin10));
  LED led_32 (.in(U20__Adder_MSB_pin13));
  _74245 U17_3st_Xceiver (
    .pin1(1'b1), .pin2(U20__Adder_MSB_pin10), .pin3(U20__Adder_MSB_pin13), .pin4(U20__Adder_MSB_pin1),
    .pin5(U20__Adder_MSB_pin4), .pin6(U21__Adder_LSB_pin10), .pin7(U21__Adder_LSB_pin13),
    .pin8(U21__Adder_LSB_pin1), .pin9(U21__Adder_LSB_pin4), .pin10(1'b0), .pin11(bussplitter_4_d0),
    .pin12(bussplitter_4_d1), .pin13(bussplitter_4_d2), .pin14(bussplitter_4_d3), .pin15(bussplitter_4_d4),
    .pin16(bussplitter_4_d5), .pin17(bussplitter_4_d6), .pin18(bussplitter_4_d7), .pin19(EO), .pin20(1'b1));
  _74157 U33__2bit_Mux (
    .pin1(U33__2bit_Mux_pin1), .pin2(U33__2bit_Mux_pin14[0]), .pin3(U33__2bit_Mux_pin3),
    .pin4(U33__2bit_Mux_pin4), .pin5(U33__2bit_Mux_pin14[1]), .pin6(U33__2bit_Mux_pin6),
    .pin7(U33__2bit_Mux_pin7), .pin8(1'b0), .pin9(U33__2bit_Mux_pin9), .pin10(U33__2bit_Mux_pin10),
    .pin11(U33__2bit_Mux_pin14[2]), .pin12(U33__2bit_Mux_pin12), .pin13(U33__2bit_Mux_pin13),
    .pin14(U33__2bit_Mux_pin14[3]), .pin15(1'b0), .pin16(1'b1));
  LED led_33 (.in(U33__2bit_Mux_pin12));
  LED led_34 (.in(U33__2bit_Mux_pin9));
  _7402 U22__NOR (
    .pin1(U22__NOR_pin1), .pin2(U20__Adder_MSB_pin4), .pin3(U20__Adder_MSB_pin1), .pin4(U22__NOR_pin4),
    .pin5(U20__Adder_MSB_pin13), .pin6(U20__Adder_MSB_pin10), .pin7(1'b0), .pin8(U21__Adder_LSB_pin4),
    .pin9(U21__Adder_LSB_pin1), .pin10(U22__NOR_pin10), .pin11(U21__Adder_LSB_pin13),
    .pin12(U21__Adder_LSB_pin10), .pin13(U22__NOR_pin13), .pin14(1'b1));
  _74173 U19__Register (
    .pin1(1'b0), .pin2(1'b0), .pin3(CF), .pin4(ZF), .pin7(CLK_t_t), .pin8(1'b0), .pin9(FI), .pin10(FI),
    .pin11(U19__Register_pin11), .pin12(U19__Register_pin12), .pin13(U19__Register_pin13),
    .pin14(U20__Adder_MSB_pin9), .pin15(CLR_t), .pin16(1'b1));  // open: pin5, pin6
  LED led_35 (.in(U33__2bit_Mux_pin7));
  LED led_36 (.in(U33__2bit_Mux_pin4));
  // NotConnected on U19__Register_pin12
  _74173 U34__register (
    .pin1(1'b0), .pin2(1'b0), .pin3(U33__2bit_Mux_pin3), .pin4(U33__2bit_Mux_pin6),
    .pin5(U33__2bit_Mux_pin10), .pin6(U33__2bit_Mux_pin13), .pin7(CLK_t_t), .pin8(1'b0), .pin9(MI),
    .pin10(MI), .pin11(U8__Reg_Upper_pin13[3]), .pin12(U8__Reg_Upper_pin13[2]),
    .pin13(U8__Reg_Upper_pin13[1]), .pin14(U8__Reg_Upper_pin13[0]), .pin15(CLR_t), .pin16(1'b1));
  _74157 _74157_1 (
    .pin1(U33__2bit_Mux_pin1), .pin2(1'b0), .pin3(1'b0), .pin5(1'b0), .pin6(1'b0), .pin8(1'b0), .pin10(1'b0),
    .pin11(1'b0), .pin12(_74157_1_pin12), .pin13(_74157_1_pin13), .pin14(_74157_1_pin14), .pin15(1'b0),
    .pin16(1'b1));  // open: pin4, pin7, pin9
  _7408 U23__AND (
    .pin1(U22__NOR_pin10), .pin2(U22__NOR_pin13), .pin3(U23__AND_pin3), .pin4(U22__NOR_pin1),
    .pin5(U22__NOR_pin4), .pin6(U23__AND_pin6), .pin7(1'b0), .pin9(1'b1), .pin10(1'b1),
    .pin11(U19__Register_pin13), .pin12(U23__AND_pin6), .pin13(U23__AND_pin3), .pin14(1'b1));  // open: pin8
  // NotConnected on U19__Register_pin11
  or or_1 (or_1_out, RI, not_1_out);
  not not_1 (not_1_out, U33__2bit_Mux_pin1);
  _7400 _7400_2 (
    .pin1(or_1_out), .pin2(CLK_t_t), .pin3(_74157_1_pin13), .pin4(1'b0), .pin5(1'b0), .pin7(1'b0),
    .pin9(1'b1), .pin10(1'b1), .pin12(1'b1), .pin13(1'b1), .pin14(1'b1));  // open: pin6, pin8, pin11
  _74245 _74245_2 (
    .pin1(1'b1), .pin2(_74245_2_pin2), .pin3(_74245_2_pin3), .pin4(_74245_2_pin4), .pin5(_74245_2_pin5),
    .pin6(_74245_2_pin6), .pin7(_74245_2_pin7), .pin8(_74245_2_pin8), .pin9(_74245_2_pin9), .pin10(1'b0),
    .pin11(_74245_2_pin11), .pin12(_74245_2_pin12), .pin13(_74245_2_pin13), .pin14(_74245_2_pin14),
    .pin15(_74245_2_pin15), .pin16(_74245_2_pin16), .pin17(_74245_2_pin17), .pin18(_74245_2_pin18),
    .pin19(RO), .pin20(1'b1));
  not not_2 (U33__2bit_Mux_pin1, PROG_EN_out);
  DipSwitch PROG_EN (.out(PROG_EN_out));
  not not_3 (_74157_1_pin14, Burn_out);
  Button Burn (.out(Burn_out));
  _7404 _7404_3 (
    .pin1(_7404_3_pin1), .pin2(_74245_2_pin2), .pin3(_7404_3_pin3), .pin4(_74245_2_pin3),
    .pin5(_7404_3_pin5), .pin6(_74245_2_pin4), .pin7(1'b0), .pin8(_74245_2_pin5), .pin9(_7404_3_pin9),
    .pin11(1'b1), .pin13(1'b1), .pin14(1'b1));  // open: pin10, pin12
  _74189 _74189_1 (
    .pin1(U33__2bit_Mux_pin4), .pin2(1'b0), .pin3(_74157_1_pin12), .pin4(_74189_1_pin4), .pin5(_7404_3_pin1),
    .pin6(_74189_1_pin6), .pin7(_7404_3_pin3), .pin8(1'b0), .pin9(_7404_3_pin5), .pin10(_74189_1_pin10),
    .pin11(_7404_3_pin9), .pin12(_74189_1_pin12), .pin13(U33__2bit_Mux_pin12), .pin14(U33__2bit_Mux_pin9),
    .pin15(U33__2bit_Mux_pin7), .pin16(1'b1));
  _74157 _74157_2 (
    .pin1(U33__2bit_Mux_pin1), .pin2(driver_1_out[7]), .pin3(_74245_2_pin18), .pin4(_74189_1_pin4),
    .pin5(driver_1_out[6]), .pin6(_74245_2_pin17), .pin7(_74189_1_pin6), .pin8(1'b0), .pin9(_74189_1_pin10),
    .pin10(_74245_2_pin16), .pin11(driver_1_out[5]), .pin12(_74189_1_pin12), .pin13(_74245_2_pin15),
    .pin14(driver_1_out[4]), .pin15(1'b0), .pin16(1'b1));
  DipSwitch dipswitch_2 (.out(U33__2bit_Mux_pin14[3]));
  DipSwitch dipswitch_3 (.out(U33__2bit_Mux_pin14[2]));
  DipSwitch dipswitch_4 (.out(U33__2bit_Mux_pin14[1]));
  LED led_37 (.in(_74245_2_pin2));
  DipSwitch dipswitch_5 (.out(U33__2bit_Mux_pin14[0]));
  LED led_38 (.in(_74245_2_pin3));
  LED led_39 (.in(_74245_2_pin4));
  DipSwitch dipswitch_6 (.out(dipswitch_6_out[7]));
  LED led_40 (.in(_74245_2_pin5));
  DipSwitch dipswitch_7 (.out(dipswitch_6_out[6]));
  DipSwitch dipswitch_8 (.out(dipswitch_6_out[5]));
  DipSwitch dipswitch_9 (.out(dipswitch_6_out[4]));
  LED led_41 (.in(_74245_2_pin6));
  LED led_42 (.in(_74245_2_pin7));
  DipSwitch dipswitch_10 (.out(dipswitch_6_out[3]));
  DipSwitch dipswitch_11 (.out(dipswitch_6_out[2]));
  DipSwitch dipswitch_12 (.out(dipswitch_6_out[1]));
  DipSwitch dipswitch_13 (.out(dipswitch_6_out[0]));
  LED led_43 (.in(_74245_2_pin8));
  LED led_44 (.in(_74245_2_pin9));
  assign driver_1_out = not_4_out ? dipswitch_6_out : 8'bz;  // Driver driver_1
  _7404 _7404_4 (
    .pin1(_7404_4_pin1), .pin2(_74245_2_pin6), .pin3(_7404_4_pin3), .pin4(_74245_2_pin7),
    .pin5(_7404_4_pin5), .pin6(_74245_2_pin8), .pin7(1'b0), .pin8(_74245_2_pin9), .pin9(_7404_4_pin9),
    .pin11(1'b1), .pin13(1'b1), .pin14(1'b1));  // open: pin10, pin12
  _74189 _74189_2 (
    .pin1(U33__2bit_Mux_pin4), .pin2(1'b0), .pin3(_74157_1_pin12), .pin4(_74189_2_pin4), .pin5(_7404_4_pin1),
    .pin6(_74189_2_pin6), .pin7(_7404_4_pin3), .pin8(1'b0), .pin9(_7404_4_pin5), .pin10(_74189_2_pin10),
    .pin11(_7404_4_pin9), .pin12(_74189_2_pin12), .pin13(U33__2bit_Mux_pin12), .pin14(U33__2bit_Mux_pin9),
    .pin15(U33__2bit_Mux_pin7), .pin16(1'b1));
  _74157 _74157_3 (
    .pin1(U33__2bit_Mux_pin1), .pin2(driver_1_out[3]), .pin3(_74245_2_pin14), .pin4(_74189_2_pin4),
    .pin5(driver_1_out[2]), .pin6(_74245_2_pin13), .pin7(_74189_2_pin6), .pin8(1'b0), .pin9(_74189_2_pin10),
    .pin10(_74245_2_pin12), .pin11(driver_1_out[1]), .pin12(_74189_2_pin12), .pin13(_74245_2_pin11),
    .pin14(driver_1_out[0]), .pin15(1'b0), .pin16(1'b1));
  not not_4 (not_4_out, U33__2bit_Mux_pin1);
  BusSplitter #(.Bits(8)) bussplitter_5 (
    .D(U8__Reg_Upper_pin13), .OE(RO), .D0(_74245_2_pin11), .D1(_74245_2_pin12), .D2(_74245_2_pin13),
    .D3(_74245_2_pin14), .D4(_74245_2_pin15), .D5(_74245_2_pin16), .D6(_74245_2_pin17), .D7(_74245_2_pin18));

  // Notes on the sheet:
  //   Refresh_display: Hz: 10
  //   RESET
  //   INSTRUCTION REGISTER
  //   REGISTER A
  //   REGISTER B
  //   Clock
  //   Output Register
  //   ALU
  //   Unsigned
  //   Signed
  //   PROGRAM COUNTER
  //   MEMORY ADDRESS REGISTER
  //   RAM
  //   Data
endmodule
