// Digital circuit clock_module.dig as structural Verilog
module clock_module (
  input  HLT,
  input  STEP_EN,
  input  STEP_in,
  input  CLK_in,
  output CLK,
  output CLK_2
);

  wire U5_AND_pin3, U5_AND_pin4, U5_AND_pin6, U5_AND_pin9, U5_AND_pin10;

  _7408 U5_AND (
    .pin1(CLK_in), .pin2(STEP_EN), .pin3(U5_AND_pin3), .pin4(U5_AND_pin4), .pin5(STEP_in),
    .pin6(U5_AND_pin6), .pin7(1'b0), .pin8(CLK), .pin9(U5_AND_pin9), .pin10(U5_AND_pin10), .pin12(1'b1),
    .pin13(1'b1), .pin14(1'b1));  // open: pin11
  _7404 U4_NOT (
    .pin1(STEP_EN), .pin2(U5_AND_pin4), .pin3(1'b0), .pin5(1'b0), .pin7(1'b0), .pin8(U5_AND_pin9),
    .pin9(HLT), .pin11(1'b1), .pin12(CLK_2), .pin13(CLK), .pin14(1'b1));  // open: pin4, pin6, pin10
  _7432 U6_OR (
    .pin1(U5_AND_pin3), .pin2(U5_AND_pin6), .pin3(U5_AND_pin10), .pin4(1'b0), .pin5(1'b0), .pin7(1'b0),
    .pin9(1'b1), .pin10(1'b1), .pin12(1'b1), .pin13(1'b1), .pin14(1'b1));  // open: pin6, pin8, pin11
  LED u_CLK (.in(CLK));
endmodule
