// Digital circuit control_logic.dig as structural Verilog
module control_logic (
  input  CF,
  input  ZF,
  input  CLK,
  input  [3:0] IR,
  output CLR,
  output CLR_2,
  output HLT,
  output MI,
  output RI,
  output RO,
  output IO,
  output II,
  output AO,
  output AI,
  output EO,
  output SU,
  output BI,
  output OI,
  output CE,
  output CO,
  output J,
  output FI,
  output [4:0] Step_ucode,
  output RST
);

  wire _7400_1_pin1, _7400_1_pin3, _7400_1_pin4, _7404_1_pin1, _7404_1_pin3, _7404_1_pin5, _7404_1_pin9,
       _7404_1_pin11, _7404_1_pin13, _7404_2_pin1, _7404_2_pin3, _7404_2_pin5, _7404_2_pin9, _7404_2_pin11,
       _74161_1_pin3, _74161_1_pin12, _74161_1_pin13, _74161_1_pin14;

  _7400 _7400_1 (
    .pin1(_7400_1_pin1), .pin2(_7400_1_pin1), .pin3(_7400_1_pin3), .pin4(_7400_1_pin4), .pin5(CLR_2),
    .pin6(_7400_1_pin1), .pin7(1'b0), .pin8(CLR), .pin9(CLR_2), .pin10(CLR_2), .pin11(CLR_2), .pin12(RST),
    .pin13(RST), .pin14(1'b1));
  _74161 _74161_1 (
    .pin1(_7400_1_pin3), .pin2(CLK), .pin3(_74161_1_pin3), .pin4(_74161_1_pin3), .pin5(_74161_1_pin3),
    .pin6(_74161_1_pin3), .pin7(1'b1), .pin8(1'b0), .pin9(1'b1), .pin10(1'b1), .pin12(_74161_1_pin12),
    .pin13(_74161_1_pin13), .pin14(_74161_1_pin14), .pin16(1'b1));  // open: pin11, pin15
  // NotConnected on _74161_1_pin3
  _74138 _74138_1 (
    .pin1(_74161_1_pin14), .pin2(_74161_1_pin13), .pin3(_74161_1_pin12), .pin4(1'b0), .pin5(1'b0),
    .pin6(1'b1), .pin8(1'b0), .pin10(_7400_1_pin4), .pin11(Step_ucode[4]), .pin12(Step_ucode[3]),
    .pin13(Step_ucode[2]), .pin14(Step_ucode[1]), .pin15(Step_ucode[0]), .pin16(1'b1));  // open: pin7, pin9
  _28c16_ucode_upper _28c16_ucode_upper_1 (
    .A0(_74161_1_pin14), .A1(_74161_1_pin13), .A2(_74161_1_pin12), .A3(IR[0]), .A4(IR[1]), .A5(IR[2]),
    .A6(IR[3]), .A7(1'b0), .A8(CF), .A9(ZF), .A10(1'b0), .nCE(1'b0), .nOE(1'b0), .nWE(1'b1), .VCC(1'b1),
    .GND(1'b0), .I_O0(_7404_1_pin13), .I_O1(_7404_1_pin11), .I_O2(_7404_1_pin9), .I_O3(_7404_1_pin5),
    .I_O4(_7404_1_pin3), .I_O5(RI), .I_O6(_7404_1_pin1), .I_O7(HLT));
  _28c16_ucode_lower _28c16_ucode_lower_1 (
    .A0(_74161_1_pin14), .A1(_74161_1_pin13), .A2(_74161_1_pin12), .A3(IR[0]), .A4(IR[1]), .A5(IR[2]),
    .A6(IR[3]), .A7(1'b0), .A8(CF), .A9(ZF), .A10(1'b0), .nCE(1'b0), .nOE(1'b0), .nWE(1'b1), .VCC(1'b1),
    .GND(1'b0), .I_O0(_7404_2_pin11), .I_O1(_7404_2_pin9), .I_O2(_7404_2_pin5), .I_O3(CE), .I_O4(OI),
    .I_O5(_7404_2_pin3), .I_O6(SU), .I_O7(_7404_2_pin1));
  _7404 _7404_1 (
    .pin1(_7404_1_pin1), .pin2(MI), .pin3(_7404_1_pin3), .pin4(RO), .pin5(_7404_1_pin5), .pin6(IO),
    .pin7(1'b0), .pin8(II), .pin9(_7404_1_pin9), .pin10(AI), .pin11(_7404_1_pin11), .pin12(AO),
    .pin13(_7404_1_pin13), .pin14(1'b1));
  _7404 _7404_2 (
    .pin1(_7404_2_pin1), .pin2(EO), .pin3(_7404_2_pin3), .pin4(BI), .pin5(_7404_2_pin5), .pin6(CO),
    .pin7(1'b0), .pin8(J), .pin9(_7404_2_pin9), .pin10(FI), .pin11(_7404_2_pin11), .pin13(1'b1), .pin14(1'b1));  // open: pin12
endmodule
