// Digital circuit output_register.dig as structural Verilog
module output_register (
  input  Refresh_display,
  input  OI,
  input  CLK,
  input  CLR,
  output [7:0] Bus,
  output [3:0] SEL_digit,
  output [7:0] Display_out
);

  wire _7476_1_pin6, _7476_1_pin10, _74273_1_pin2, _74273_1_pin5, _74273_1_pin6, _74273_1_pin9,
       _74273_1_pin11, _74273_1_pin12, _74273_1_pin15, _74273_1_pin16, _74273_1_pin19, dipswitch_1_out,
       not_1_out;

  not not_1 (not_1_out, CLR);
  _28c16_DisplayOut _28c16_displayout_1 (
    .A0(_74273_1_pin2), .A1(_74273_1_pin5), .A2(_74273_1_pin6), .A3(_74273_1_pin9), .A4(_74273_1_pin12),
    .A5(_74273_1_pin15), .A6(_74273_1_pin16), .A7(_74273_1_pin19), .A8(_7476_1_pin6), .A9(_7476_1_pin10),
    .A10(dipswitch_1_out), .nCE(1'b0), .nOE(1'b0), .nWE(1'b1), .VCC(1'b1), .GND(1'b0), .I_O0(Display_out[6]),
    .I_O1(Display_out[5]), .I_O2(Display_out[4]), .I_O3(Display_out[3]), .I_O4(Display_out[2]),
    .I_O5(Display_out[1]), .I_O6(Display_out[0]), .I_O7(Display_out[7]));
  _74273 _74273_1 (
    .pin1(not_1_out), .pin2(_74273_1_pin2), .pin3(Bus[0]), .pin4(Bus[1]), .pin5(_74273_1_pin5),
    .pin6(_74273_1_pin6), .pin7(Bus[2]), .pin8(Bus[3]), .pin9(_74273_1_pin9), .pin10(1'b0),
    .pin11(_74273_1_pin11), .pin12(_74273_1_pin12), .pin13(Bus[4]), .pin14(Bus[5]), .pin15(_74273_1_pin15),
    .pin16(_74273_1_pin16), .pin17(Bus[6]), .pin18(Bus[7]), .pin19(_74273_1_pin19), .pin20(1'b1));
  DipSwitch dipswitch_1 (.out(dipswitch_1_out));
  _7476 _7476_1 (
    .pin1(Refresh_display), .pin2(1'b1), .pin3(1'b1), .pin4(1'b1), .pin5(1'b1), .pin6(_7476_1_pin6),
    .pin7(1'b1), .pin8(1'b1), .pin9(1'b1), .pin10(_7476_1_pin10), .pin12(1'b1), .pin13(1'b0),
    .pin14(_7476_1_pin6), .pin16(1'b1));  // open: pin11, pin15
  _7408 _7408_1 (
    .pin1(CLK), .pin2(OI), .pin3(_74273_1_pin11), .pin4(1'b0), .pin5(1'b0), .pin7(1'b0), .pin9(1'b1),
    .pin10(1'b1), .pin12(1'b1), .pin13(1'b1), .pin14(1'b1));  // open: pin6, pin8, pin11
  Seven_Seg #(.commonCathode("true")) seven_seg_1 (
    .a(Display_out[0]), .b(Display_out[1]), .c(Display_out[2]), .d(Display_out[3]), .e(Display_out[4]),
    .f(Display_out[5]), .g(Display_out[6]), .dp(Display_out[7]), .common(SEL_digit[3]));
  _74139 _74139_1 (
    .pin1(1'b0), .pin2(_7476_1_pin6), .pin3(_7476_1_pin10), .pin4(SEL_digit[0]), .pin5(SEL_digit[1]),
    .pin6(SEL_digit[2]), .pin7(SEL_digit[3]), .pin8(1'b0), .pin13(1'b1), .pin14(1'b1), .pin15(1'b1),
    .pin16(1'b1));  // open: pin9, pin10, pin11, pin12
  Seven_Seg #(.commonCathode("true")) seven_seg_2 (
    .a(Display_out[0]), .b(Display_out[1]), .c(Display_out[2]), .d(Display_out[3]), .e(Display_out[4]),
    .f(Display_out[5]), .g(Display_out[6]), .dp(Display_out[7]), .common(SEL_digit[2]));
  Seven_Seg #(.commonCathode("true")) seven_seg_3 (
    .a(Display_out[0]), .b(Display_out[1]), .c(Display_out[2]), .d(Display_out[3]), .e(Display_out[4]),
    .f(Display_out[5]), .g(Display_out[6]), .dp(Display_out[7]), .common(SEL_digit[1]));
  Seven_Seg #(.commonCathode("true")) seven_seg_4 (
    .a(Display_out[0]), .b(Display_out[1]), .c(Display_out[2]), .d(Display_out[3]), .e(Display_out[4]),
    .f(Display_out[5]), .g(Display_out[6]), .dp(Display_out[7]), .common(SEL_digit[0]));

  // Notes on the sheet:
  //   Refresh_display: Hz: 50000
  //   contents of 28C16_DISPLAY (hex, n*v repeats v):
  //   7e,30,6d,79,33,5b,5f,70,7f,7b,7e,30,6d,79,33,5b,5f,70,7f,7b,7e,30,6d,79,33,5b,5f, 70,7f,7b,
  //   7e,30,6d,79,33,5b,5f,70,7f,7b,7e,30,6d,79,33,5b,5f,70,7f,7b,7e,30,6d,79, 33,5b,5f,70,7f,7b,
  //   7e,30,6d,79,33,5b,5f,70,7f,7b,7e,30,6d,79,33,5b,5f,70,7f,7b,7e, 30,6d,79,33,5b,5f,70,7f,7b,
  //   7e,30,6d,79,33,5b,5f,70,7f,7b,7e,30,6d,79,33,5b,5f,70, 7f,7b,7e,30,6d,79,33,5b,5f,70,7f,7b,
  //   7e,30,6d,79,33,5b,5f,70,7f,7b,7e,30,6d,79,33, 5b,5f,70,7f,7b,7e,30,6d,79,33,5b,5f,70,7f,7b,
  //   7e,30,6d,79,33,5b,5f,70,7f,7b,7e,30, 6d,79,33,5b,5f,70,7f,7b,7e,30,6d,79,33,5b,5f,70,7f,7b,
  //   7e,30,6d,79,33,5b,5f,70,7f, 7b,7e,30,6d,79,33,5b,5f,70,7f,7b,7e,30,6d,79,33,5b,5f,70,7f,7b,
  //   7e,30,6d,79,33,5b, 5f,70,7f,7b,7e,30,6d,79,33,5b,5f,70,7f,7b,7e,30,6d,79,33,5b,5f,70,7f,7b,
  //   7e,30,6d, 79,33,5b,5f,70,7f,7b,7e,30,6d,79,33,5b,7e,7e,7e,7e,7e,7e,7e,7e,7e,7e,30,30,30,30,
  //    30,30,30,30,30,30,6d,6d,6d,6d,6d,6d,6d,6d,6d,6d,79,79,79,79,79,79,79,79,79,79,33, 33,33,33,
  //   33,33,33,33,33,33,5b,5b,5b,5b,5b,5b,5b,5b,5b,5b,5f,5f,5f,5f,5f,5f,5f,5f, 5f,5f,70,70,70,70,
  //   70,70,70,70,70,70,7f,7f,7f,7f,7f,7f,7f,7f,7f,7f,7b,7b,7b,7b,7b, 7b,7b,7b,7b,7b,7e,7e,7e,7e,
  //   7e,7e,7e,7e,7e,7e,30,30,30,30,30,30,30,30,30,30,6d,6d, 6d,6d,6d,6d,6d,6d,6d,6d,79,79,79,79,
  //   79,79,79,79,79,79,33,33,33,33,33,33,33,33,33, 33,5b,5b,5b,5b,5b,5b,5b,5b,5b,5b,5f,5f,5f,5f,
  //   5f,5f,5f,5f,5f,5f,70,70,70,70,70,70, 70,70,70,70,7f,7f,7f,7f,7f,7f,7f,7f,7f,7f,7b,7b,7b,7b,
  //   7b,7b,7b,7b,7b,7b,7e,7e,7e, 7e,7e,7e,7e,7e,7e,7e,30,30,30,30,30,30,30,30,30,30,6d,6d,6d,6d,
  //   6d,6d,6d,6d,6d,6d, 79,79,79,79,79,79,79,79,79,79,33,33,33,33,33,33,33,33,33,33,5b,5b,5b,5b,
  //   5b,5b,7e, 7e,7e,7e,7e,7e,7e,7e,7e,7e,7e,7e,7e,7e,7e,7e,7e,7e,7e,7e,7e,7e,7e,7e,7e,7e,7e,7e,
  //    7e,7e,7e,7e,7e,7e,7e,7e,7e,7e,7e,7e,7e,7e,7e,7e,7e,7e,7e,7e,7e,7e,7e,7e,7e,7e,7e, 7e,7e,7e,
  //   7e,7e,7e,7e,7e,7e,7e,7e,7e,7e,7e,7e,7e,7e,7e,7e,7e,7e,7e,7e,7e,7e,7e,7e, 7e,7e,7e,7e,7e,7e,
  //   7e,7e,7e,7e,7e,7e,7e,7e,7e,7e,7e,7e,30,30,30,30,30,30,30,30,30, 30,30,30,30,30,30,30,30,30,
  //   30,30,30,30,30,30,30,30,30,30,30,30,30,30,30,30,30,30, 30,30,30,30,30,30,30,30,30,30,30,30,
  //   30,30,30,30,30,30,30,30,30,30,30,30,30,30,30, 30,30,30,30,30,30,30,30,30,30,30,30,30,30,30,
  //   30,30,30,30,30,30,30,30,30,30,30,30, 30,30,30,30,30,30,30,30,30,30,6d,6d,6d,6d,6d,6d,6d,6d,
  //   6d,6d,6d,6d,6d,6d,6d,6d,6d, 6d,6d,6d,6d,6d,6d,6d,6d,6d,6d,6d,6d,6d,6d,6d,6d,6d,6d,6d,6d,6d,
  //   6d,6d,6d,6d,6d,6d, 6d,6d,6d,6d,6d,6d,6d,6d,6d,6d,6d,6d,0,0,0,0,0,0,0,0,0,0,0,0,0,0,0,0,0,0,
  //   0,0,0,0,0, 0,0,0,0,0,0,0,0,0,0,0,0,0,0,0,0,0,0,0,0,0,0,0,0,0,0,0,0,0,0,0,0,0,0,0,0,0,0,0,0,
  //   0, 0,0,0,0,0,0,0,0,0,0,0,0,0,0,0,0,0,0,0,0,0,0,0,0,0,0,0,0,0,0,0,0,0,0,0,0,0,0,0,0,0, 0,0,0,
  //   0,0,0,0,0,0,0,0,0,0,0,0,0,0,0,0,0,0,0,0,0,0,0,0,0,0,0,0,0,0,0,0,0,0,0,0,0,0, 0,0,0,0,0,0,0,
  //   0,0,0,0,0,0,0,0,0,0,0,0,0,0,0,0,0,0,0,0,0,0,0,0,0,0,0,0,0,0,0,0,0,0, 0,0,0,0,0,0,0,0,0,0,0,
  //   0,0,0,0,0,0,0,0,0,0,0,0,0,0,0,0,0,0,0,0,0,0,0,0,0,0,0,0,0,0, 0,0,0,0,0,0,0,0,0,0,0,0,0,0,0,
  //   0,0,0,0,0,0,0,0,0,0,0,0,0,7f,70,5f,5b,33,79,6d,30,7e, 7b,7f,70,5f,5b,33,79,6d,30,7e,7b,7f,70,
  //   5f,5b,33,79,6d,30,7e,7b,7f,70,5f,5b,33,79, 6d,30,7e,7b,7f,70,5f,5b,33,79,6d,30,7e,7b,7f,70,
  //   5f,5b,33,79,6d,30,7e,7b,7f,70,5f, 5b,33,79,6d,30,7e,7b,7f,70,5f,5b,33,79,6d,30,7e,7b,7f,70,
  //   5f,5b,33,79,6d,30,7e,7b, 7f,70,5f,5b,33,79,6d,30,7e,7b,7f,70,5f,5b,33,79,6d,30,7e,7b,7f,70,
  //   5f,5b,33,79,6d, 30,7e,7b,7f,70,5f,5b,33,79,6d,30,7e,30,6d,79,33,5b,5f,70,7f,7b,7e,30,6d,79,
  //   33,5b, 5f,70,7f,7b,7e,30,6d,79,33,5b,5f,70,7f,7b,7e,30,6d,79,33,5b,5f,70,7f,7b,7e,30,6d, 79,
  //   33,5b,5f,70,7f,7b,7e,30,6d,79,33,5b,5f,70,7f,7b,7e,30,6d,79,33,5b,5f,70,7f,7b, 7e,30,6d,79,
  //   33,5b,5f,70,7f,7b,7e,30,6d,79,33,5b,5f,70,7f,7b,7e,30,6d,79,33,5b,5f, 70,7f,7b,7e,30,6d,79,
  //   33,5b,5f,70,7f,7b,7e,30,6d,79,33,5b,5f,70,7f,7b,7e,30,6d,79, 33,5b,5f,70,6d,6d,6d,6d,6d,6d,
  //   6d,6d,6d,30,30,30,30,30,30,30,30,30,30,7e,7e,7e,7e, 7e,7e,7e,7e,7e,7e,7b,7b,7b,7b,7b,7b,7b,
  //   7b,7b,7b,7f,7f,7f,7f,7f,7f,7f,7f,7f,7f,70, 70,70,70,70,70,70,70,70,70,5f,5f,5f,5f,5f,5f,5f,
  //   5f,5f,5f,5b,5b,5b,5b,5b,5b,5b,5b, 5b,5b,33,33,33,33,33,33,33,33,33,33,79,79,79,79,79,79,79,
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endmodule
