// Digital circuit program_counter.dig as structural Verilog
module program_counter (
  input  CO,
  input  CLK,
  input  CLR,
  input  CE,
  input  J,
  output [3:0] LEDs,
  output [7:0] Bus
);

  wire _74161_1_pin1, _74245_1_pin11, _74245_1_pin12, _74245_1_pin13, _74245_1_pin14, _74245_1_pin15,
       _74245_1_pin16, _74245_1_pin17, _74245_1_pin18;

  _74245 _74245_1 (
    .pin1(1'b1), .pin2(1'b0), .pin3(1'b0), .pin4(1'b0), .pin5(1'b0), .pin6(LEDs[0]), .pin7(LEDs[1]),
    .pin8(LEDs[2]), .pin9(LEDs[3]), .pin10(1'b0), .pin11(_74245_1_pin11), .pin12(_74245_1_pin12),
    .pin13(_74245_1_pin13), .pin14(_74245_1_pin14), .pin15(_74245_1_pin15), .pin16(_74245_1_pin16),
    .pin17(_74245_1_pin17), .pin18(_74245_1_pin18), .pin19(CO), .pin20(1'b1));
  _74161 _74161_1 (
    .pin1(_74161_1_pin1), .pin2(CLK), .pin3(_74245_1_pin14), .pin4(_74245_1_pin13), .pin5(_74245_1_pin12),
    .pin6(_74245_1_pin11), .pin7(CE), .pin8(1'b0), .pin9(J), .pin10(CE), .pin11(LEDs[3]), .pin12(LEDs[2]),
    .pin13(LEDs[1]), .pin14(LEDs[0]), .pin16(1'b1));  // open: pin15
  not not_1 (_74161_1_pin1, CLR);
  BusSplitter #(.Bits(8)) bussplitter_1 (
    .D(Bus), .OE(CO), .D0(_74245_1_pin14), .D1(_74245_1_pin13), .D2(_74245_1_pin12), .D3(_74245_1_pin11),
    .D4(_74245_1_pin15), .D5(_74245_1_pin16), .D6(_74245_1_pin17), .D7(_74245_1_pin18));

  // Notes on the sheet:
  //   CO: default 1
  //   CLR: default 1
  //   J: default 1
endmodule
