// Digital circuit register_A.dig as structural Verilog
module register_A (
  input  CLK,
  input  AO,
  input  AI,
  input  CLR,
  output [7:0] BUS,
  output [7:0] A_out
);

  wire bussplitter_1_d0, bussplitter_1_d1, bussplitter_1_d2, bussplitter_1_d3, bussplitter_1_d4,
       bussplitter_1_d5, bussplitter_1_d6, bussplitter_1_d7;

  BusSplitter #(.Bits(8)) bussplitter_1 (
    .D(BUS), .OE(AO), .D0(bussplitter_1_d0), .D1(bussplitter_1_d1), .D2(bussplitter_1_d2),
    .D3(bussplitter_1_d3), .D4(bussplitter_1_d4), .D5(bussplitter_1_d5), .D6(bussplitter_1_d6),
    .D7(bussplitter_1_d7));
  _74245 U7_3st_Xceiver (
    .pin1(1'b1), .pin2(A_out[7]), .pin3(A_out[6]), .pin4(A_out[5]), .pin5(A_out[4]), .pin6(A_out[3]),
    .pin7(A_out[2]), .pin8(A_out[1]), .pin9(A_out[0]), .pin10(1'b0), .pin11(bussplitter_1_d0),
    .pin12(bussplitter_1_d1), .pin13(bussplitter_1_d2), .pin14(bussplitter_1_d3), .pin15(bussplitter_1_d4),
    .pin16(bussplitter_1_d5), .pin17(bussplitter_1_d6), .pin18(bussplitter_1_d7), .pin19(AO), .pin20(1'b1));
  LED led_1 (.in(A_out[7]));
  LED led_2 (.in(A_out[6]));
  LED led_3 (.in(A_out[5]));
  LED led_4 (.in(A_out[4]));
  LED led_5 (.in(A_out[3]));
  LED led_6 (.in(A_out[2]));
  LED led_7 (.in(A_out[1]));
  LED led_8 (.in(A_out[0]));
  _74173 U8__Reg_Upper (
    .pin1(1'b0), .pin2(1'b0), .pin3(A_out[7]), .pin4(A_out[6]), .pin5(A_out[5]), .pin6(A_out[4]), .pin7(CLK),
    .pin8(1'b0), .pin9(AI), .pin10(AI), .pin11(bussplitter_1_d4), .pin12(bussplitter_1_d5),
    .pin13(bussplitter_1_d6), .pin14(bussplitter_1_d7), .pin15(CLR), .pin16(1'b1));
  _74173 U9__Reg_Lower (
    .pin1(1'b0), .pin2(1'b0), .pin3(A_out[3]), .pin4(A_out[2]), .pin5(A_out[1]), .pin6(A_out[0]), .pin7(CLK),
    .pin8(1'b0), .pin9(AI), .pin10(AI), .pin11(bussplitter_1_d0), .pin12(bussplitter_1_d1),
    .pin13(bussplitter_1_d2), .pin14(bussplitter_1_d3), .pin15(CLR), .pin16(1'b1));
  // Pins of 1 and 8 bits meet at BUS

  // Notes on the sheet:
  //   AO: default 1
  //   AI: default 1
endmodule
