// Digital circuit register_B.dig as structural Verilog
module register_B (
  input  CLK,
  input  BO,
  input  BI,
  input  CLR,
  output [7:0] BUS,
  output [7:0] B_out
);

  wire bussplitter_1_d0, bussplitter_1_d1, bussplitter_1_d2, bussplitter_1_d3, bussplitter_1_d4,
       bussplitter_1_d5, bussplitter_1_d6, bussplitter_1_d7;

  BusSplitter #(.Bits(8)) bussplitter_1 (
    .D(BUS), .OE(BO), .D0(bussplitter_1_d0), .D1(bussplitter_1_d1), .D2(bussplitter_1_d2),
    .D3(bussplitter_1_d3), .D4(bussplitter_1_d4), .D5(bussplitter_1_d5), .D6(bussplitter_1_d6),
    .D7(bussplitter_1_d7));
  _74245 U7_3st_Xceiver (
    .pin1(1'b1), .pin2(B_out[7]), .pin3(B_out[6]), .pin4(B_out[5]), .pin5(B_out[4]), .pin6(B_out[3]),
    .pin7(B_out[2]), .pin8(B_out[1]), .pin9(B_out[0]), .pin10(1'b0), .pin11(bussplitter_1_d0),
    .pin12(bussplitter_1_d1), .pin13(bussplitter_1_d2), .pin14(bussplitter_1_d3), .pin15(bussplitter_1_d4),
    .pin16(bussplitter_1_d5), .pin17(bussplitter_1_d6), .pin18(bussplitter_1_d7), .pin19(BO), .pin20(1'b1));
  LED led_1 (.in(B_out[7]));
  LED led_2 (.in(B_out[6]));
  LED led_3 (.in(B_out[5]));
  LED led_4 (.in(B_out[4]));
  LED led_5 (.in(B_out[3]));
  LED led_6 (.in(B_out[2]));
  LED led_7 (.in(B_out[1]));
  LED led_8 (.in(B_out[0]));
  _74173 U8__Reg_Upper (
    .pin1(1'b0), .pin2(1'b0), .pin3(B_out[7]), .pin4(B_out[6]), .pin5(B_out[5]), .pin6(B_out[4]), .pin7(CLK),
    .pin8(1'b0), .pin9(BI), .pin10(BI), .pin11(bussplitter_1_d4), .pin12(bussplitter_1_d5),
    .pin13(bussplitter_1_d6), .pin14(bussplitter_1_d7), .pin15(CLR), .pin16(1'b1));
  _74173 U9__Reg_Lower (
    .pin1(1'b0), .pin2(1'b0), .pin3(B_out[3]), .pin4(B_out[2]), .pin5(B_out[1]), .pin6(B_out[0]), .pin7(CLK),
    .pin8(1'b0), .pin9(BI), .pin10(BI), .pin11(bussplitter_1_d0), .pin12(bussplitter_1_d1),
    .pin13(bussplitter_1_d2), .pin14(bussplitter_1_d3), .pin15(CLR), .pin16(1'b1));
  // Pins of 1 and 8 bits meet at BUS

  // Notes on the sheet:
  //   BO: default 1
  //   BI: default 1
endmodule
