// Digital circuit register_Instruction.dig as structural Verilog
module register_Instruction (
  input  CLK,
  input  IO,
  input  II,
  input  CLR,
  output [7:0] BUS,
  output [7:0] I_out
);

  wire bussplitter_1_d0, bussplitter_1_d1, bussplitter_1_d2, bussplitter_1_d3, bussplitter_1_d4,
       bussplitter_1_d5, bussplitter_1_d6, bussplitter_1_d7, U7_3st_Xceiver_pin6, U7_3st_Xceiver_pin7,
       U7_3st_Xceiver_pin8, U7_3st_Xceiver_pin9;

  BusSplitter #(.Bits(8)) bussplitter_1 (
    .D(BUS), .OE(IO), .D0(bussplitter_1_d0), .D1(bussplitter_1_d1), .D2(bussplitter_1_d2),
    .D3(bussplitter_1_d3), .D4(bussplitter_1_d4), .D5(bussplitter_1_d5), .D6(bussplitter_1_d6),
    .D7(bussplitter_1_d7));
  _74245 U7_3st_Xceiver (
    .pin1(1'b1), .pin2(I_out[3]), .pin3(I_out[2]), .pin4(I_out[1]), .pin5(I_out[0]),
    .pin6(U7_3st_Xceiver_pin6), .pin7(U7_3st_Xceiver_pin7), .pin8(U7_3st_Xceiver_pin8),
    .pin9(U7_3st_Xceiver_pin9), .pin10(1'b0), .pin11(bussplitter_1_d0), .pin12(bussplitter_1_d1),
    .pin13(bussplitter_1_d2), .pin14(bussplitter_1_d3), .pin15(bussplitter_1_d4), .pin16(bussplitter_1_d5),
    .pin17(bussplitter_1_d6), .pin18(bussplitter_1_d7), .pin19(IO), .pin20(1'b1));
  LED led_1 (.in(I_out[3]));
  LED led_2 (.in(I_out[2]));
  LED led_3 (.in(I_out[1]));
  LED led_4 (.in(I_out[0]));
  LED led_5 (.in(U7_3st_Xceiver_pin6));
  LED led_6 (.in(U7_3st_Xceiver_pin7));
  LED led_7 (.in(U7_3st_Xceiver_pin8));
  LED led_8 (.in(U7_3st_Xceiver_pin9));
  _74173 U8__Reg_Upper (
    .pin1(1'b0), .pin2(1'b0), .pin3(I_out[3]), .pin4(I_out[2]), .pin5(I_out[1]), .pin6(I_out[0]), .pin7(CLK),
    .pin8(1'b0), .pin9(II), .pin10(II), .pin11(bussplitter_1_d4), .pin12(bussplitter_1_d5),
    .pin13(bussplitter_1_d6), .pin14(bussplitter_1_d7), .pin15(CLR), .pin16(1'b1));
  _74173 U9__Reg_Lower (
    .pin1(1'b0), .pin2(1'b0), .pin3(U7_3st_Xceiver_pin6), .pin4(U7_3st_Xceiver_pin7),
    .pin5(U7_3st_Xceiver_pin8), .pin6(U7_3st_Xceiver_pin9), .pin7(CLK), .pin8(1'b0), .pin9(II), .pin10(II),
    .pin11(bussplitter_1_d0), .pin12(bussplitter_1_d1), .pin13(bussplitter_1_d2), .pin14(bussplitter_1_d3),
    .pin15(CLR), .pin16(1'b1));
  // Pins of 1 and 8 bits meet at BUS
  // Pins of 4 and 8 bits meet at I_out

  // Notes on the sheet:
  //   IO: default 1
  //   II: default 1
endmodule
