// Digital circuit register_MAD.dig as structural Verilog
module register_MAD (
  input  MI,
  input  CLK,
  input  CLR,
  input  PROG_in,
  input  [7:0] Bus_in,
  output [3:0] A_out,
  output PROG_out
);

  wire U33__2bit_Mux_pin3, U33__2bit_Mux_pin6, U33__2bit_Mux_pin10, U33__2bit_Mux_pin13;

  PullUp pullup_1 (.out(PROG_in));
  _74157 U33__2bit_Mux (
    .pin1(PROG_in), .pin2(Bus_in[0]), .pin3(U33__2bit_Mux_pin3), .pin4(A_out[0]), .pin5(Bus_in[1]),
    .pin6(U33__2bit_Mux_pin6), .pin7(A_out[1]), .pin8(1'b0), .pin9(A_out[2]), .pin10(U33__2bit_Mux_pin10),
    .pin11(Bus_in[2]), .pin12(A_out[3]), .pin13(U33__2bit_Mux_pin13), .pin14(Bus_in[3]), .pin15(1'b0),
    .pin16(1'b1));
  LED led_1 (.in(A_out[3]));
  LED led_2 (.in(A_out[2]));
  LED led_3 (.in(A_out[1]));
  LED led_4 (.in(A_out[0]));
  _74173 U34__register (
    .pin1(1'b0), .pin2(1'b0), .pin3(U33__2bit_Mux_pin3), .pin4(U33__2bit_Mux_pin6),
    .pin5(U33__2bit_Mux_pin10), .pin6(U33__2bit_Mux_pin13), .pin7(CLK), .pin8(1'b0), .pin9(MI), .pin10(MI),
    .pin11(Bus_in[3]), .pin12(Bus_in[2]), .pin13(Bus_in[1]), .pin14(Bus_in[0]), .pin15(CLR), .pin16(1'b1));

  assign PROG_out = PROG_in;

  // Notes on the sheet:
  //   MI: default 1
endmodule
